# Fritzing sketch Fritzing (saved by Fritzing 0.9.3b)
breadboards: 1

parts:
  Q1 = NPN-Transistor [package="TO92 [THT]"]
  R1 = Resistor [tolerance=±5% resistance=330 package=THT]
  OMRON1 = OMRON PCB Power Relay – G5LE [part_number="G5LE-1\n" package=THT]
  LED1 = smd LED [color="Red (633nm)" package="1206 [SMD]"]

nets:
  N1: Q1.E, OMRON1.COIL2
  N2: Q1.B, R1.Pin_1
  N3: Q1.C, OMRON1.C
  N4: R1.Pin_0, LED1.cathode

notes:
  ESP8266-01
  GPIO2
  Q1 = BC5xx - NPN
  R1 = 330 ohms
  LED1 = LED 5mm qq cor
  RELE = Bobina 5Vcc
  Coletor -> Bobina rele
  Emissor ->GND
  Base ->R1->AnodoLed
  Catodo LED ->GPIO2
  5VCC Fonte GND
  Regulador 3V3.
